# Fritzing sketch receiver (saved by Fritzing 0.9.10b)
circuit board: 6.9cm x 4.7cm

parts:
  U2 = mystery part, 3 pins [chip_label="433 Transmitter"]
  CONN1 = USB connector [package=THT]
  U1 = ESP32-38PinWide [part_number=ESP32]

nets:
  N1: U2.pin1, U1.GPIO34
  N2: U2.pin2, U1.3.3
  GND: U2.pin3, CONN1.GND, CONN1.chassis5, CONN1.chassis6, U1.GND
  5V: CONN1.5V, U1.VIN

notes:
  alicescfernandes

custom parts:
  ESP32-38PinWide: Generic 38-Pin ESP32 with wide format (only access to one side of pins on a breadboard) based on Stephen Lilley's HiLetgo ESP-WROOM-32 ESP32 ESP-32S Development Board.
