# Fritzing sketch transmitter (saved by Fritzing 0.9.10b)
circuit board: 4.60601cm x 2.55665cm
stripboards: 2

parts:
  J1 = female pin header, 3 pins [form="♀ (female)"]
  R1 = Resistor [tolerance=±5% resistance=1M power=0.25 package=THT]
  Mod1 = seeeduino-xiao
  J2 = female pin header, 1 pin [form="♀ (female)"]
  J3 = female pin header, 1 pin [form="♀ (female)"]

nets:
  N1: J1.pin1, Mod1.D7
  N2: J1.pin2, Mod1.5V
  N3: J1.pin3, R1.Pin_1, Mod1.GND, J3.pin1
  N4: R1.Pin_0, Mod1.D5, J2.pin1

notes:
  alicescfernandes

custom parts:
  seeeduino-xiao: Seeeduino XIAO processor board.
